# Fritzing sketch t (saved by Fritzing 0.9.3b)
breadboards: 1

parts:
  Componente1 = Arduino BT
  Q1 = NPN-Transistor [package="TO92 [THT]"]
  R1 = Resistor [tolerance=±5% resistance=220 package=THT]

nets:
  N1: Componente1.PWM_D6, Q1.B, R1.Pin_0
  N2: Componente1.GND, Q1.E, Q1.C
  N3: Componente1.5V, R1.Pin_1
