# Fritzing sketch c (saved by Fritzing 0.9.3b)

parts:
  Componente1 = Arduino BT
  Componente2 = Gas Sensor Breakout Board

nets:
  N1: Componente1.A0, Componente2.A2
  N2: Componente1.GND, Componente2.B2
